# Fritzing sketch wiring diagram (saved by Fritzing 0.9.9b)

parts:
  Ac_Power = Power plug
  Part1 = IFR520 MOS module [package=THT]
  Part2 = IFR520 MOS module [package=THT]
  Part3 = IFR520 MOS module [package=THT]
  Part4 = IFR520 MOS module [package=THT]
  Mod1 = Raspberry Pi Pico
  M1 = RioRand LM2596
  HLK-PM3 = HLK-PM12 [part_number=HLK-PM12]
  Part5 = IFR520 MOS module [package=THT]
  Part6 = IFR520 MOS module [package=THT]
  Part7 = IFR520 MOS module [package=THT]
  Part8 = IFR520 MOS module [package=THT]
  Part9 = IFR520 MOS module [package=THT]
  Part10 = IFR520 MOS module [package=THT]
  Part11 = IFR520 MOS module [package=THT]
  Part12 = IFR520 MOS module [package=THT]
  Part13 = IFR520 MOS module [package=THT]
  Part14 = IFR520 MOS module [package=THT]
  Part15 = IFR520 MOS module [package=THT]
  Part16 = IFR520 MOS module [package=THT]
  M2 = DC Motor
  M3 = DC Motor
  M4 = DC Motor
  M5 = DC Motor
  M6 = DC Motor
  M7 = DC Motor
  M8 = DC Motor
  M9 = DC Motor
  M10 = DC Motor
  M11 = DC Motor
  M12 = DC Motor
  M13 = DC Motor
  M14 = DC Motor
  M17 = DC Motor
  M15 = DC Motor
  M16 = DC Motor
  HLK-PM4 = HLK-PM01
  Ac_Power1 = Power plug
  Mod2 = Raspberry Pi 4B  # not connected
  Mod3 = Raspberry Pi Pico
  Part17 = IFR520 MOS module [package=THT]
  M18 = DC Motor
  8_Channel_Relay1 = 8 Channel Power Relay
  L1 = Solenoid
  L2 = Solenoid
  L3 = Solenoid
  L4 = Solenoid
  R1 = Heating Pad
  R2 = Heating Pad
  YF-S201_Flow_Meter1 = YF-S201 Water Flow Meter
  YF-S201_Flow_Meter2 = YF-S201 Water Flow Meter
  Water_Level_Sensor1 = Water Level Sensor
  Water_Level_Sensor2 = Water Level Sensor

nets:
  N1: Ac_Power.VCC, HLK-PM3.AC_1
  N2: Ac_Power.GND, HLK-PM3.AC_2
  N3: Part1.SIG, Mod1.pin_1
  VCC: Part1.VCC, Part2.VCC, Part3.VCC, Part4.VCC, Mod1.pin_36, Part5.VCC, Part6.VCC, Part7.VCC, Part8.VCC, Part9.VCC, Part10.VCC, Part11.VCC, Part12.VCC, Part13.VCC, Part14.VCC, Part15.VCC, Part16.VCC, Part17.VCC, 8_Channel_Relay1.VCC
  GND: Part1.GND, Part2.GND, Part3.GND, Part4.GND, Mod1.pin_3, Mod1.pin_8, Mod1.pin_13, Mod1.pin_18, Mod1.pin_23, Mod1.pin_38, Part6.SIG, Part9.GND, Part9.VIN, Part10.GND, Part11.GND, Part12.GND, Part12.VIN, Part13.GND, Part13.VIN, Part14.GND, Part15.GND, Part16.GND, Part16.VIN, M2.pin_1, M3.pin_1, M4.pin_1, M5.pin_1, M11.pin_1, M11.pin_2, M12.pin_1, M12.pin_2, M14.pin_1, M14.pin_2, M17.pin_1, M17.pin_2, Part17.GND, M18.pin_1
  N4: Part1.V+, Part2.V+, Part3.V+, Part4.V+, M1.Pin_3, Part5.V+, Part6.V+, Part7.V+, Part8.V+, Part9.V+, Part10.V+, Part11.V+, Part12.V+, Part13.V+, Part14.V+, Part15.V+, Part16.V+, Part17.V+
  N5: Part1.V-, Part2.V-, Part3.V-, Part4.V-, M1.Pin_4, Part5.V-, Part6.V-, Part7.V-, Part8.V-, Part9.V-, Part10.V-, Part11.V-, Part12.V-, Part13.V-, Part14.V-, Part15.V-, Part16.V-, Part17.V-
  N6: Part1.VIN, M2.pin_2
  N7: Part2.SIG, Mod1.pin_2
  N8: Part2.VIN, M3.pin_2
  N9: Part3.SIG, Mod1.pin_4
  N10: Part3.VIN, M4.pin_2
  N11: Part4.SIG, Mod1.pin_5
  N12: Part4.VIN, M5.pin_2
  N13: Mod1.pin_6, Part8.SIG
  N14: Mod1.pin_7, Part7.SIG
  GND_2: Mod1.pin_9, Part5.GND, Part5.VIN, Part6.GND, Part6.VIN, Part7.GND, Part7.VIN, Part8.GND, Part8.VIN, M6.pin_1, M6.pin_2, M7.pin_1, M7.pin_2, M8.pin_1, M8.pin_2, M9.pin_1, M9.pin_2
  N15: Mod1.pin_10, Part5.SIG
  N16: Mod1.pin_11, Part12.SIG
  N17: Mod1.pin_12, Part11.SIG
  N18: Mod1.pin_14, Part10.SIG
  N19: Mod1.pin_15, Part9.SIG
  N20: Mod1.pin_16, Part16.SIG
  N21: Mod1.pin_17, Part15.SIG
  N22: Mod1.pin_19, Part14.SIG
  N23: Mod1.pin_20, Part13.SIG
  N24: Mod1.pin_21, 8_Channel_Relay1.IN1
  N25: Mod1.pin_22, 8_Channel_Relay1.IN2
  N26: Mod1.pin_24, 8_Channel_Relay1.IN3
  N27: Mod1.pin_25, 8_Channel_Relay1.IN4
  N28: Mod1.pin_37, Part17.SIG
  N29: M1.Pin_1, HLK-PM3.+Vo
  N30: M1.Pin_2, HLK-PM3.-Vo
  N31: Part10.VIN, M10.pin_1, M10.pin_2
  N32: Part11.VIN, M13.pin_2
  N33: Part14.VIN, M16.pin_1, M16.pin_2
  N34: Part15.VIN, M15.pin_2
  N35: HLK-PM4.AC#0, Ac_Power1.VCC
  N36: HLK-PM4.AC#1, Ac_Power1.GND
  GND_3: HLK-PM4.-Vo, 8_Channel_Relay1.GND, YF-S201_Flow_Meter1.GND, YF-S201_Flow_Meter2.GND, Water_Level_Sensor1.GND, Water_Level_Sensor2.GND
  VCC_2: HLK-PM4.+Vo, 8_Channel_Relay1.JD-VCC, YF-S201_Flow_Meter1.VCC, YF-S201_Flow_Meter2.VCC, Water_Level_Sensor2.VCC
  N37: Mod3.pin_1, YF-S201_Flow_Meter2.SIG
  N38: Mod3.pin_2, YF-S201_Flow_Meter1.SIG
  N39: Part17.VIN, M18.pin_2
  N40: 8_Channel_Relay1.COM#22, L1.pin1
  N41: 8_Channel_Relay1.NO#23, L1.pin2
  N42: 8_Channel_Relay1.COM#25, L2.pin1
  N43: 8_Channel_Relay1.NO#26, L2.pin2
  N44: 8_Channel_Relay1.COM#28, L3.pin1
  N45: 8_Channel_Relay1.NO#29, L3.pin2
  N46: 8_Channel_Relay1.COM#31, L4.pin1
  N47: 8_Channel_Relay1.NO#32, L4.pin2
  N48: 8_Channel_Relay1.COM#34, R1.pin_0
  N49: 8_Channel_Relay1.NO#35, R1.pin_1
  N50: 8_Channel_Relay1.COM#37, R2.pin_0
  N51: 8_Channel_Relay1.NO#38, R2.pin_1

notes:
  Ac Power
  OUTPUT : 24VDC
  Peristalic Pumps
  IN : 24v | OUT : 12v
  water pump
  Pico 1 : control
  Pico 2 : sensors
  Solenoid 1
  Solenoid 2
  Solenoid 3
  Solenoid 4
  Heating pad bin 1
  Heating pad bin 2
  5v Relay switch
  Water Sensors
  Hall Effect Sensor

custom parts:
  Raspberry Pi Pico: Raspberry Pi Pico. Based around the RP2040 microcontroller the Pico is a low cost microcontroller device bringing Raspberry Pi quality, cost, and easy of use to the microcontroller space. Jan 2021, Split part in to two versions: tht (this one) and SMD. This one will drill holes for a .1 in header in pcb to allow plugging in the module as well as providing pads to solder the module to the top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
  8 Channel Power Relay: An 8 channel power relay. The module operates at 5V.
  Heating Pad: A thermoresistant material with an embeded conductor that dissipates electrical energy into heat.
  YF-S201 Water Flow Meter: The YF-S201 Flow Meter. The input voltage is 5V to 24V (DC).
  Water Level Sensor: A water level sensor. This sensor operates at 3V to 5V. The Sig (signal) pin outputs an analogue signal that is in proportion to the amount of water in contact with the sensor.
